# Fritzing sketch Pomodoro (saved by Fritzing 0.9.6b)
breadboards: 1

parts:
  LCD1 = LCD screen  # not connected
  R1 = Resistor [tolerance=±5% resistance=220 package="2512 [SMD]"]
  R2 = Resistor [tolerance=±5% resistance=220 package="2512 [SMD]"]
  R3 = Resistor [tolerance=±5% resistance=220 package="2512 [SMD]"]
  Componente1 = Arduino Uno (Rev3) - ICSP
  LED1 = LED - 3mm [color="Green (555nm)" current=0.030 package="3 mm [THT]"]
  LED2 = LED - 3mm [color="Yellow (595nm)" current=0.030 package="3 mm [THT]"]
  LED3 = LED - 3mm [color="Red (633nm)" current=0.030 package="3 mm [THT]"]
  S1 = Pushbutton [package="[THT]"]
  J1 = female pin header, 4 pins [form="♀ (female)"]
  J1_2 = female alternating pin header, 4 pins [form="♀ (female)"]
  J1_3 = female pin header, 4 pins [form="♀ (female)"]

nets:
  N1: R1.Pin_0, Componente1.D8, LED2.anode
  N2: R1.Pin_1, R2.Pin_1, R3.Pin_1, Componente1.GND, S1.Pin_1, S1.Pin_2, J1.pin2, J1_2.pin2, J1_3.pin2
  N3: R2.Pin_0, Componente1.D9_PWM, LED1.anode
  N4: R3.Pin_0, Componente1.D10_PWM/SS, LED3.anode
  N5: Componente1.A4/SDA, J1.pin3, J1_2.pin3, J1_3.pin3
  N6: Componente1.A5/SCL, J1.pin4, J1_2.pin4, J1_3.pin4
  N7: Componente1.D4, S1.Pin_3, S1.Pin_4
  N8: Componente1.5V, J1.pin1, J1_2.pin1, J1_3.pin1

notes:
  SCL
  GND
  SDA
  VCC
  220Ω
